// Logisim project Circuit.circ as structural Verilog: 9 circuits, main circuit main
// 0
module main (
);

  wire B0, B1, B2, B3, B4, B5, B6, B7, B8, B9, BDiv, BMult, BSub, BSum, not_1_out, NumberEn, OpEn;
  wire [3:0] Number, register_1_q;
  wire [24:0] Op;

  Button _1 (.out(B1));
  Button _4 (.out(B4));
  Button _7 (.out(B7));
  Button _2 (.out(B2));
  Button _5 (.out(B5));
  Button _8 (.out(B8));
  Button _0 (.out(B0));
  operation_control operation_control (.sum(BSum), .sub(BSub), .mult(BMult), .div(BDiv), .Data(Op), .Enable(OpEn));
  number_control number_control (
    ._0(B0), ._1(B1), ._2(B2), ._3(B3), ._4(B4), ._5(B5), ._6(B6), ._7(B7), ._8(B8), ._9(B9), .Data(Number),
    .Enable(NumberEn));
  Button button (.out(BSum));
  Button _3 (.out(B3));
  Button button_2 (.out(BSub));
  Button _6 (.out(B6));
  Button x (.out(BMult));
  Button _9 (.out(B9));
  Button button_3 (.out(BDiv));
  Hex_Digit_Display hex_digit_display_1 ();  // open: value, dp
  DotMatrix #(.matrixrows(5)) dotmatrix_1 (
    .col0(Op[24:20]), .col1(Op[19:15]), .col2(Op[14:10]), .col3(Op[9:5]), .col4(Op[4:0]));
  Hex_Digit_Display hex_digit_display_2 ();  // open: value, dp
  // Probe on Number
  not not_1 (not_1_out, NumberEn);
  Register #(.width(4), .trigger("low")) register_1 (
    .D(Number), .en(NumberEn), .Q(register_1_q), .clk(not_1_out));  // open: clr
  // Probe on register_1_q
endmodule

module latchSR (
  input  Set,
  input  Reset,
  output out_3
);

  wire and_1_out, and_2_out, not_2_out;

  and and_1 (and_1_out, Set, not_2_out);
  and and_2 (and_2_out, out_3, Reset);
  not not_1 (out_3, and_1_out);
  not not_2 (not_2_out, and_2_out);
endmodule

module latchD (
  input  D,
  input  Enable,
  output out_3
);

  wire and_1_out, and_2_out, not_1_out, not_2_out, not_3_out;

  not not_1 (not_1_out, D);
  and and_1 (and_1_out, D, Enable);
  not not_2 (not_2_out, and_1_out);
  and and_2 (and_2_out, Enable, not_1_out);
  not not_3 (not_3_out, and_2_out);
  latchSR latchsr_1 (.Set(not_2_out), .Reset(not_3_out), .out_3(out_3));
endmodule

module flip_flop (
  input  D,
  input  Enable,
  input  Clock,
  output out_4
);

  wire and_1_out, latchd_1_out_3, not_1_out;

  and and_1 (and_1_out, Enable, Clock);
  not not_1 (not_1_out, Clock);
  latchD latchd_1 (.D(D), .Enable(and_1_out), .out_3(latchd_1_out_3));
  latchD latchd_2 (.D(latchd_1_out_3), .Enable(not_1_out), .out_3(out_4));
endmodule

module registradores (
  input  Clock,
  input  Enable,
  input  Reset,
  input  [3:0] AddresA,
  input  [3:0] AddresB,
  input  [15:0] Data,
  output [15:0] DataA,
  output [15:0] DataB
);

  wire en0, en1, en2, en3, en4, en5, en6, en7, en8, en9, en10, en11, en12, en13, en14, en15;
  wire [15:0] out0, out1, out2, out3, out4, out5, out6, out7, out8, out9, out10, out11, out12, out13, out14,
       out15;

  Demultiplexer #(.select(4)) demultiplexer_1 (
    .out0(en0), .out1(en1), .out2(en2), .out3(en3), .out4(en4), .out5(en5), .out6(en6), .out7(en7),
    .out8(en8), .out9(en9), .out10(en10), .out11(en11), .out12(en12), .out13(en13), .out14(en14),
    .out15(en15), .in(Enable), .sel(AddresA));  // open: en
  Register #(.width(16)) register_1 (.D(Data), .en(en0), .Q(out0), .clk(Clock), .clr(Reset));
  Register #(.width(16)) register_2 (.D(Data), .en(en1), .Q(out1), .clk(Clock), .clr(Reset));
  Register #(.width(16)) register_3 (.D(Data), .en(en3), .Q(out3), .clk(Clock), .clr(Reset));
  Register #(.width(16)) register_4 (.D(Data), .en(en4), .Q(out4), .clk(Clock), .clr(Reset));
  Register #(.width(16)) register_5 (.D(Data), .en(en5), .Q(out5), .clk(Clock), .clr(Reset));
  Register #(.width(16)) register_6 (.D(Data), .en(en6), .Q(out6), .clk(Clock), .clr(Reset));
  Register #(.width(16)) register_7 (.D(Data), .en(en7), .Q(out7), .clk(Clock), .clr(Reset));
  Register #(.width(16)) register_8 (.D(Data), .en(en8), .Q(out8), .clk(Clock), .clr(Reset));
  Multiplexer #(.select(4), .width(16)) multiplexer_1 (
    .in0(out0), .in1(out1), .in2(out2), .in3(out3), .in4(out4), .in5(out5), .in6(out6), .in7(out7),
    .in8(out8), .in9(out9), .in10(out10), .in11(out11), .in12(out12), .in13(out13), .in14(out14),
    .in15(out15), .out(DataA), .sel(AddresA));  // open: en
  Multiplexer #(.select(4), .width(16)) multiplexer_2 (
    .in0(out0), .in1(out1), .in2(out2), .in3(out3), .in4(out4), .in5(out5), .in6(out6), .in7(out7),
    .in8(out8), .in9(out9), .in10(out10), .in11(out11), .in12(out12), .in13(out13), .in14(out14),
    .in15(out15), .out(DataB), .sel(AddresB));  // open: en
  Register #(.width(16)) register_9 (.D(Data), .en(en9), .Q(out9), .clk(Clock), .clr(Reset));
  Register #(.width(16)) register_10 (.D(Data), .en(en10), .Q(out10), .clk(Clock), .clr(Reset));
  Register #(.width(16)) register_11 (.D(Data), .en(en11), .Q(out11), .clk(Clock), .clr(Reset));
  Register #(.width(16)) register_12 (.D(Data), .en(en12), .Q(out12), .clk(Clock), .clr(Reset));
  Register #(.width(16)) register_13 (.D(Data), .en(en15), .Q(out15), .clk(Clock), .clr(Reset));
  Register #(.width(16)) register_14 (.D(Data), .en(en2), .Q(out2), .clk(Clock), .clr(Reset));
  Register #(.width(16)) register_15 (.D(Data), .en(en13), .Q(out13), .clk(Clock), .clr(Reset));
  Register #(.width(16)) register_16 (.D(Data), .en(en14), .Q(out14), .clk(Clock), .clr(Reset));

  // Other names for the same wires on the sheet: addA[3:0] = AddresA; addB[3:0] = AddresB; clk = Clock; en = Enable;
  //   rst = Reset
endmodule

module ULA (
  input  [15:0] IA,
  input  [15:0] IB,
  input  [3:0] Control,
  output [15:0] out_4
);

  wire [15:0] AND, ANegatorOut, Decrement, Div, Increment, LeftShiftOut, Mult, OR, RightShiftOut, Sub, Sum,
       XOR;

  Adder #(.width(16)) adder_1 (.a(IA), .b(IB), .out(Sum));  // open: cin, cout
  Subtractor #(.width(16)) subtractor_1 (.a(IA), .b(IB), .out(Sub));  // open: bin, bout
  Multiplier #(.width(16)) multiplier_1 (.a(IA), .b(IB), .out(Mult));  // open: cin, cout
  Divider #(.width(16)) divider_1 (.a(IA), .b(IB), .out(Div));  // open: upper, rem
  Adder #(.width(16)) adder_2 (.a(IA), .b(16'h1), .out(Increment));  // open: cin, cout
  Subtractor #(.width(16)) subtractor_2 (.a(IA), .b(16'h1), .out(Decrement));  // open: bin, bout
  Shifter #(.width(16), .shift("lr")) shifter_1 (.in(IA), .\dist (IB[3:0]), .out(RightShiftOut));
  Shifter #(.width(16)) shifter_2 (.in(IA), .\dist (IB[3:0]), .out(LeftShiftOut));
  Negator #(.width(16)) negator_1 (.in(IA), .out(ANegatorOut));
  assign AND = IA & IB;  // AND_Gate and_1, 16 bits wide
  assign OR = IA | IB;  // OR_Gate or_1, 16 bits wide
  assign XOR = IA ^ IB;  // XOR_Gate xor_1, 16 bits wide
  Multiplexer #(.select(4), .width(16)) multiplexer_1 (
    .in0(Sum), .in1(Sub), .in2(Mult), .in3(Div), .in4(Increment), .in5(Decrement), .in6(AND), .in7(OR),
    .in8(XOR), .in9(RightShiftOut), .in10(LeftShiftOut), .in11(ANegatorOut), .out(out_4), .sel(Control));  // open: in12, in13, in14, in15, en
endmodule

module number_control (
  input  _0,
  input  _1,
  input  _2,
  input  _3,
  input  _4,
  input  _5,
  input  _6,
  input  _7,
  input  _8,
  input  _9,
  output [3:0] Data,
  output Enable
);

  wire [3:0] Out0, Out1, Out2, Out3, Out4, Out5, Out6, Out7, Out8, Out9;

  Multiplexer #(.width(4)) multiplexer_1 (.in0(4'b0000), .in1(4'b0000), .out(Out0), .sel(_0));  // open: en
  Multiplexer #(.width(4)) multiplexer_2 (.in0(4'b0000), .in1(4'b0100), .out(Out4), .sel(_4));  // open: en
  Multiplexer #(.width(4)) multiplexer_3 (.in0(4'b0000), .in1(4'b1000), .out(Out8), .sel(_8));  // open: en
  Multiplexer #(.width(4)) multiplexer_4 (.in0(4'b0000), .in1(4'b0001), .out(Out1), .sel(_1));  // open: en
  Multiplexer #(.width(4)) multiplexer_5 (.in0(4'b0000), .in1(4'b0101), .out(Out5), .sel(_5));  // open: en
  Multiplexer #(.width(4)) multiplexer_6 (.in0(4'b0000), .in1(4'b1001), .out(Out9), .sel(_9));  // open: en
  Multiplexer #(.width(4)) multiplexer_7 (.in0(4'b0000), .in1(4'b0010), .out(Out2), .sel(_2));  // open: en
  Multiplexer #(.width(4)) multiplexer_8 (.in0(4'b0000), .in1(4'b0110), .out(Out6), .sel(_6));  // open: en
  assign Data = Out0 | Out1 | Out2 | Out3 | Out4 | Out5 | Out6 | Out7 | Out8 | Out9;  // OR_Gate or_1, 4 bits wide
  or or_2 (Enable, _0, _1, _2, _3, _4, _5, _6, _7, _8, _9);
  Multiplexer #(.width(4)) multiplexer_9 (.in0(4'b0000), .in1(4'b0011), .out(Out3), .sel(_3));  // open: en
  Multiplexer #(.width(4)) multiplexer_10 (.in0(4'b0000), .in1(4'b0111), .out(Out7), .sel(_7));  // open: en

  // Other names for the same wires on the sheet: I0 = _0; I1 = _1; I2 = _2; I3 = _3; I4 = _4; I5 = _5; I6 = _6;
  //   I7 = _7; I8 = _8; I9 = _9
endmodule

module operation_control (
  input  sum,
  input  sub,
  input  mult,
  input  div,
  output [24:0] Data,
  output Enable
);

  wire [24:0] divOut, multOut, subOut, sumOut;

  Multiplexer #(.width(25)) multiplexer_1 (.in0({25{1'b0}}), .in1(25'h23880), .out(sumOut), .sel(sum));  // open: en
  Multiplexer #(.width(25)) multiplexer_2 (.in0({25{1'b0}}), .in1(25'h21080), .out(subOut), .sel(sub));  // open: en
  Multiplexer #(.width(25)) multiplexer_3 (.in0({25{1'b0}}), .in1(25'h25480), .out(multOut), .sel(mult));  // open: en
  Multiplexer #(.width(25)) multiplexer_4 (.in0({25{1'b0}}), .in1(25'h51140), .out(divOut), .sel(div));  // open: en
  assign Data = sumOut | subOut | multOut | divOut;  // OR_Gate or_1, 25 bits wide
  or or_2 (Enable, sum, sub, mult, div);
endmodule

module processor (
  input  [3:0] num_data,
  input  num_en,
  input  [1:0] op_data,
  input  op_en,
  output [3:0] NumA,
  output [3:0] NumB,
  output [24:0] operator_symbol,
  output [1:0] operator
);
endmodule
